# Fritzing sketch quelab-rfid (saved by Fritzing 0.9.3b)
circuit board: 9.11298cm x 5.65539cm
breadboards: 1

parts:
  Part1 = Arduino Nano (Rev3.0)
  Part2 = RDM6300-ANT
  R1 = Resistor [tolerance=±5% resistance=200 package=THT]
  R2 = Resistor [tolerance=±1% resistance=4.85k package=THT]
  D2 = Schottky Diode [part_number=1N5817 package="300 mil [THT]"]
  Q1 = TRANSISTOR_NPN [package=to-92-ammo]
  R3 = Resistor [tolerance=±5% resistance=47 package=THT]
  R4 = Resistor [tolerance=±5% resistance=200 package=THT]
  R5 = Resistor [tolerance=±5% resistance=200 package=THT]
  RED_LED = LEDs [package=led10mm]
  Yellow_LED = LEDs [package=led10mm]
  R6 = Resistor [tolerance=±5% resistance=200 package=THT]
  R7 = Resistor [tolerance=±5% resistance=2.2k package=THT]
  125_kHz_RFID_module1 = RDM6300
  J2 = male pin header, 3 pins [form="♂ (male)"]
  D1 = Schottky Diode [part_number=1N5817 package="300 mil [THT]"]
  Green_LED = LEDs [package=led10mm]
  S1 = Reed switch [package=THT]
  S2 = Pushbutton [package=THT]

nets:
  N1: Part1.GND, Q1.E, R4.Pin_0, R5.Pin_0, 125_kHz_RFID_module1.GND#60, J2.pin3, S1.pin_2, S2.leg1
  N2: Part1.D2, 125_kHz_RFID_module1.TX, 125_kHz_RFID_module1.GND#66
  N3: Part1.D4, R1.Pin_0
  N4: Part1.D5, RED_LED.A
  N5: Part1.D6, Green_LED.A
  N6: Part1.D7, R7.Pin_0, J2.pin2, S1.pin_1
  N7: Part1.D8, D2.anode
  N8: Part1.3V3, D1.anode
  N9: Part2.ANT1, 125_kHz_RFID_module1.ANT1
  N10: Part2.ANT2, 125_kHz_RFID_module1.ANT2
  N11: R1.Pin_1, Q1.B
  N12: R2.Pin_0, D1.cathode
  N13: R2.Pin_1, D2.cathode, R3.Pin_0, J2.pin1, S2.leg0
  N14: Q1.C, R3.Pin_1
  N15: R4.Pin_1, Green_LED.C
  N16: R5.Pin_1, RED_LED.C
  N17: Yellow_LED.C, 125_kHz_RFID_module1.LED
  N18: Yellow_LED.A, R6.Pin_1
  N19: R6.Pin_0, 125_kHz_RFID_module1.+5V#65
  N20: R7.Pin_1, 125_kHz_RFID_module1.+5V#61

custom parts:
  RDM6300-ANT: Antenna
  RDM6300: 125 kHz RFID module (serial interface)
